# Fritzing sketch semaforo (saved by Fritzing 0.9.3b)
breadboards: 1

parts:
  U1 = NodeMCU V1.0
  R1 = Resistor [tolerance=±5% resistance=220 package=THT]
  R2 = Resistor [tolerance=±5% resistance=220 package=THT]
  R3 = Resistor [tolerance=±5% resistance=220 package=THT]
  LED1 = LED - 3mm [color="Red (633nm)" package="3 mm [THT]"]
  LED2 = LED - 3mm [color="Orange (620nm)" package="3 mm [THT]"]
  LED3 = LED - 3mm [color="Green (555nm)" package="3 mm [THT]"]

nets:
  N1: U1.D1, R2.Pin_0
  N2: U1.GND, LED1.cathode, LED2.cathode, LED3.cathode
  N3: U1.D5, R1.Pin_0
  N4: U1.D8, R3.Pin_0
  N5: R1.Pin_1, LED2.anode
  N6: R2.Pin_1, LED1.anode
  N7: R3.Pin_1, LED3.anode

custom parts:
  NodeMCU V1.0: ESP9266 based NodeMCU
