# Fritzing sketch telegrafo (saved by Fritzing 0.9.3b)
breadboards: 1

parts:
  U1 = NodeMCU V1.0
  J1 = Piezo Speaker
  S1 = Pushbutton [package="[THT]"]
  R1 = Resistor [tolerance=±5% resistance=220 package="1206 [SMD]"]
  R2 = Resistor [tolerance=±5% resistance=220 package="1206 [SMD]"]

nets:
  N1: U1.D1, J1.pin2
  N2: U1.3V3, S1.Pin_1, S1.Pin_2
  N3: U1.GND, R1.Pin_0, R2.Pin_0
  N4: U1.D5, S1.Pin_3, S1.Pin_4, R1.Pin_1
  N5: J1.pin1, R2.Pin_1

custom parts:
  NodeMCU V1.0: ESP9266 based NodeMCU
